// Logisim project control_logic.circ as structural Verilog: 1 circuit, main circuit control_logic
module control_logic (
  input  [31:0] inst,
  input  BrEq,
  input  BrLt,
  output PCSel,
  output RegWEn,
  output [2:0] ImmSel,
  output BrUn,
  output ASel,
  output BSel,
  output [3:0] ALUSel,
  output MemRW,
  output [1:0] WBSel,
  output CSRSel,
  output CSRWen
);


  assign ALUSel = 4'b0001;
  assign ASel = 1'b0;
  assign BrUn = 1'b0;
  assign BSel = 1'b0;
  assign CSRSel = 1'b0;
  assign CSRWen = 1'b0;
  assign ImmSel = 3'b001;
  assign MemRW = 1'b1;
  assign PCSel = 1'b1;
  assign RegWEn = 1'b1;
  assign WBSel = 2'b00;

  // Notes on the sheet:
  //   INPUTS to your circuit
  //   DON'T CHANGE THE LOCATIONS OF THE INPUTS AND OUTPUTS!
  //   OUTPUT from your circuit
endmodule
