// Logisim project cpu.circ as structural Verilog: 1 circuit, main circuit cpu
module cpu (
  input  clk,
  input  [31:0] INSTRUCTION,
  input  [31:0] READ_DATA,
  output [31:0] WRITE_ADDRESS,
  output [31:0] PROGRAM_COUNTER,
  output [31:0] ra,
  output [31:0] sp,
  output [31:0] t0,
  output [31:0] t1,
  output [31:0] t2,
  output [31:0] s0,
  output [31:0] s1,
  output [31:0] a0,
  output [31:0] tohost,
  output [3:0] WRITE_ENABLE,
  output [31:0] WRITE_DATA
);

  wire ASel, BSel, RegWEn;
  wire [2:0] ImmSel;
  wire [3:0] ALUSel;
  wire [31:0] adder_1_out, ALU_A, ALU_B, Imm0, inst_ex, pc_ex, read_data1, read_data2, wb;

  Adder #(.width(32)) adder_1 (.a(PROGRAM_COUNTER), .b(32'h4), .out(adder_1_out));  // open: cin, cout
  Register #(.width(32)) PC (.D(adder_1_out), .en(1'b1), .clk(clk), .Q(PROGRAM_COUNTER));  // open: clr
  Register #(.width(32)) register_1 (.D(PROGRAM_COUNTER), .en(1'b1), .clk(clk), .Q(pc_ex));  // open: clr
  Register #(.width(32)) register_2 (.D(INSTRUCTION), .en(1'b1), .clk(clk), .Q(inst_ex));  // open: clr
  control_logic control_logic_1 (
    .RegWEn(RegWEn), .ImmSel(ImmSel), .ASel(ASel), .BSel(BSel), .ALUSel(ALUSel), .inst(inst_ex));  // open: CSRWen, PCSel, BrUn, MemRW, WBSel, CSRSel, BrEq, BrLt
  imm_gen imm_gen_1 (.inst(inst_ex), .ImmSel(ImmSel), .imm(Imm0));
  regfile regfile_1 (
    .rs1(inst_ex[19:15]), .rs2(inst_ex[24:20]), .rd(inst_ex[11:7]), .Write_Data(wb), .RegWEn(RegWEn),
    .clk(clk), .ra(ra), .sp(sp), .t0(t0), .t1(t1), .t2(t2), .s0(s0), .s1(s1), .a0(a0),
    .Read_Data_1(read_data1), .Read_Data_2(read_data2));
  // branch_comp branch_comp_1: pin names not known
  Multiplexer #(.enable("false"), .width(32)) multiplexer_1 (.in0(read_data1), .in1(pc_ex), .out(ALU_A), .sel(ASel));
  alu alu_1 (.Result(wb), .A(ALU_A), .B(ALU_B), .ALUSel(ALUSel));
  csr csr_1 (.CSR_address({12{1'b0}}), .CSR_din({32{1'b0}}), .CSR_WE(1'b0), .clk(clk), .tohost(tohost));
  Multiplexer #(.enable("false"), .width(32)) multiplexer_2 (.in0(read_data2), .in1(Imm0), .out(ALU_B), .sel(BSel));

  assign WRITE_ADDRESS = {32{1'b0}};
  assign WRITE_DATA = {32{1'b0}};
  assign WRITE_ENABLE = 4'b0000;

  // Other names for the same wires on the sheet: rd0[4:0] = inst_ex[11:7]; rs1[4:0] = inst_ex[19:15];
  //   rs2[4:0] = inst_ex[24:20]

  // Notes on the sheet:
  //   Output to IMEM
  //   IMEM (do **NOT** move this)
  //   Inputs from IMEM
  //   It is OK to move the PC, RegFile, ALU, MEM, Branch Comp, Imm Gen, and Control Logic to wherever is most convenient for you when constructing your CPU, and to delete this text
  //   Inputs/Outputs for testing. Do **NOT** move these.
  //   Outputs To DMEM
  //   DMEM (do **NOT** move this)
  //   Inputs From DMEM
endmodule
